// Logisim project somador-subtrator.circ as structural Verilog: 3 circuits, main circuit main
module main (
  input  Subtrator,
  input  [15:0] in_2,
  input  [15:0] in_3,
  input  Write_Enable,
  output [15:0] out_5
);

  wire button_1_out, clock_1_out;
  wire [15:0] somador_subtrator_1_out_4, ula_1_out_5, ula_2_out_5;

  Clock clock_1 (.out(clock_1_out));
  Button button_1 (.out(button_1_out));
  ULA ula_1 (.in_1(in_2), .Write_Enable(Write_Enable), .Clock(clock_1_out), .Reset(button_1_out), .out_5(ula_1_out_5));
  ULA ula_2 (.in_1(in_3), .Write_Enable(Write_Enable), .Clock(clock_1_out), .Reset(button_1_out), .out_5(ula_2_out_5));
  somador_subtrator somador_subtrator_1 (
    .C_in(Subtrator), .in_2(ula_1_out_5), .in_3(ula_2_out_5), .out_4(somador_subtrator_1_out_4));  // open: C_out
  ULA ula_3 (
    .in_1(somador_subtrator_1_out_4), .Write_Enable(Write_Enable), .Clock(clock_1_out), .Reset(button_1_out),
    .out_5(out_5));

  // Notes on the sheet:
  //   Entrada A
  //   Entrada B
  //   Clock
  //   Reset
  //   Registrador 1
  //   Registrador 2
  //   Opereção
  //   Registrador 3
  //   Saída
endmodule

module ULA (
  input  [15:0] in_1,
  input  Write_Enable,
  input  Clock,
  input  Reset,
  output [15:0] out_5
);

  Register #(.width(16)) register_1 (.D(in_1), .en(Write_Enable), .Q(out_5), .clk(Clock), .clr(Reset));

  // Notes on the sheet:
  //   Entrada
  //   Unidade Lógica e Aritmética
  //   Saída
endmodule

module somador_subtrator (
  input  C_in,
  input  [15:0] in_2,
  input  [15:0] in_3,
  output [15:0] out_4,
  output C_out
);

  wire adder_1_cout;
  wire [15:0] multiplexer_1_out, not_1_out;

  // Probe on in_2
  // Probe on in_3
  Multiplexer #(.width(16)) multiplexer_1 (
    .in0(in_3), .in1(not_1_out), .out(multiplexer_1_out), .sel(C_in));  // open: en
  assign not_1_out = ~in_3;  // NOT_Gate not_1, 16 bits wide
  Adder adder_1 (.a(in_2[7:0]), .b(multiplexer_1_out[7:0]), .out(out_4[7:0]), .cin(C_in), .cout(adder_1_cout));
  Adder adder_2 (.a(in_2[15:8]), .b(multiplexer_1_out[15:8]), .out(out_4[15:8]), .cin(adder_1_cout), .cout(C_out));
  // Probe on out_4

  // Notes on the sheet:
  //   Entrada A
  //   Entrada B
  //   Saída
endmodule
